# Fritzing sketch arduino_schematic (saved by Fritzing 0.9.3b)
circuit board: 8.46667cm x 5.64444cm
breadboards: 1

parts:
  Componente1 = Arduino Mega ADK (Rev3)
  Part1 = KY-026 Flame Sensor Module [package="Breakout board"]
  Part2 = KY-015 Temperature & Humidity Sensor Module [package="Breakout board"]
  Part3 = KY-018 Photoresistor Module [package="Breakout board"]
  Part4 = KY-013 Analog Temperature Sensor Module [package="Breakout board"]

nets:
  N1: Componente1.A0, Part4.S
  N2: Componente1.A2, Part3.S
  N3: Componente1.A4, Part1.A0
  GND: Componente1.GND, Part1.G, Part2.-, Part3.-, Part4.-
  VIN: Componente1.IOREF, Componente1.5V, Part1.+, Part2.Vin, Part3.Vin, Part4.Vin
  N4: Componente1.D22, Part2.S

custom parts:
  KY-026 Flame Sensor Module: KEYES KY-026 Arduino Flame Sensor Module reacts iin the presence of fire.
  KY-015 Temperature & Humidity Sensor Module: KY-015 temperature and humidity sensor module, provides a low-latency serial interface to measure humidity and temperature.
  KY-018 Photoresistor Module: KY-018 Photoresistor module, used to measure light intensity. It can determine the presence or absence of light.
  KY-013 Analog Temperature Sensor Module: KY-013 Analog Temperature Sensor module, measures ambient temperature based on resistance of the thermistor.
